# Fritzing sketch AndroidFritzingSketch (saved by Fritzing 0.9.3b)
breadboards: 1

parts:
  R1 = Resistor [tolerance=±5% resistance=220 package="2512 [SMD]"]
  LED1 = LED - 5mm [color="Red (633nm)" package="5 mm [THT]"]
  S1 = Pushbutton [package="[THT]"]
  Raspberry_Pi_1 = Raspberry Pi 3 [part_number=RPI-3-V1.2]  # not connected

nets:
  N1: R1.Pin_0, LED1.cathode
  N2: R1.Pin_1, S1.Pin_1, S1.Pin_2
  N3: S1.Pin_3, S1.Pin_4
